// Logisim project Group 6_PROJECT phase 2.circ as structural Verilog: 5 circuits, main circuit main
module main (
  input  [3:0] Direct_write,
  input  R,
  input  [1:0] Input_address,
  input  STORE,
  input  LOAD,
  input  S2,
  input  S1,
  input  S0,
  input  Cin,
  input  Load_store_Data,
  input  X,
  input  [3:0] in_12,
  input  Z,
  output [3:0] A,
  output [3:0] out_15,
  output [3:0] B,
  output [3:0] OUTPUT_RESULT
);

  wire [3:0] multiplexer_1_out, ram_1_data;

  Multiplexer #(.width(4)) multiplexer_1 (
    .in0(Direct_write), .in1(OUTPUT_RESULT), .out(multiplexer_1_out), .sel(R));  // open: en
  Multiplexer #(.width(4)) multiplexer_2 (.in0(in_12), .in1(out_15), .out(B), .sel(Z));  // open: en
  RAM #(.addrWidth(2), .dataWidth(4), .bus("separate")) ram_1 (
    .addr(Input_address), .din(multiplexer_1_out), .data(ram_1_data), .str(STORE), .clk(Load_store_Data),
    .ld(LOAD));  // open: sel, clr
  Multiplexer #(.select(2), .width(4)) multiplexer_3 (
    .in0(A), .in1(ram_1_data), .in2(A), .in3(A), .out(A), .sel({X, LOAD}));  // open: en
  Multiplexer #(.select(2), .width(4)) multiplexer_4 (
    .in0(out_15), .in1(out_15), .in2(out_15), .in3(ram_1_data), .out(out_15), .sel({X, LOAD}));  // open: en
  ALU alu_1 (
    .A3(A[3]), .A2(A[2]), .A1(A[1]), .A0(A[0]), .B3(B[3]), .B2(B[2]), .B1(B[1]), .B0(B[0]), .Cin(Cin),
    .Result(OUTPUT_RESULT), .S2(S2), .S1(S1), .S0(S0));

  // Notes on the sheet:
  //   To directly write into memory:
  //   Y:
  //   Select 0 to input A, select 1 to input B
  //   Before starting make sure, R, Y, X,Z are disabled
  //   6. Finally, disable both button R and Load/Store
  //   Address
  //   Disable button R, input address, and write input to direct write. Followed by, enabling STORE and LOad/Store Data
  //   Storing/Writing
  //   Steps to use (read from memory and carry out operations):
  //   1. Choose if adress A/address B data is read using button X
  //   2. Input the address to be accessed using Input address (Y), make sure to disable Load/Store if not already,to load it,enable Load
  //   If B is immediate/ constant choose 0, else choose 1
  //   3. If B is a constant/ immediate operand, then choose 0, in button Z, else ENABLE BUTTON Z
  //   5. To write the ouput to memory, first enable Storing/Writing Button (R), then input address, followed by enabling Store (str) , and then Load/Store Button
  //   Memory
  //   4. At the right, select inputs for the operations can be viewed (S2,S1,S0,Cin). Use the buttons to input each operation
  //   (ld)
endmodule

module adder (
  input  Ai,
  input  Bi,
  input  Ci,
  input  S1,
  input  S0,
  output S,
  output C
);

  wire and_1_out, and_2_out, and_3_out, multiplexer_1_out, not_1_out, xor_1_out;

  not not_1 (not_1_out, Bi);
  Multiplexer #(.select(2)) multiplexer_1 (
    .in0(1'b0), .in1(Bi), .in2(not_1_out), .in3(1'b1), .out(multiplexer_1_out), .sel({S1, S0}));  // open: en
  xor xor_1 (xor_1_out, Ai, multiplexer_1_out);
  and and_1 (and_1_out, Ai, multiplexer_1_out);
  and and_2 (and_2_out, multiplexer_1_out, Ci);
  and and_3 (and_3_out, Ai, Ci);
  xor xor_2 (S, xor_1_out, Ci);
  or or_1 (C, and_1_out, and_2_out, and_3_out);
endmodule

module shifter (
  input  A3,
  input  A2,
  input  A1,
  input  A0,
  input  So,
  input  Cin,
  output out_7,
  output out_8,
  output out_9,
  output out_10
);

  Multiplexer #(.select(2)) multiplexer_1 (
    .in0(A3), .in1(1'b0), .in2(A2), .out(out_7), .sel({So, Cin}));  // open: in3, en
  Multiplexer #(.select(2)) multiplexer_2 (
    .in0(A2), .in1(A3), .in2(A1), .out(out_8), .sel({So, Cin}));  // open: in3, en
  Multiplexer #(.select(2)) multiplexer_3 (
    .in0(A1), .in1(A2), .in2(A0), .out(out_10), .sel({So, Cin}));  // open: in3, en
  Multiplexer #(.select(2)) multiplexer_4 (
    .in0(A0), .in1(A1), .in2(1'b0), .out(out_9), .sel({So, Cin}));  // open: in3, en
endmodule

module \logic  (
  input  A3,
  input  A2,
  input  A1,
  input  A0,
  input  B3,
  input  S0,
  input  B2,
  input  B1,
  input  Cin,
  input  B0,
  output [3:0] out_11
);

  wire [3:0] and_1_out, not_1_out, or_1_out, xor_1_out;

  assign and_1_out = {A3, A2, A1, A0} & {B3, B2, B1, B0};  // AND_Gate and_1, 4 bits wide
  assign or_1_out = {A3, A2, A1, A0} | {B3, B2, B1, B0};  // OR_Gate or_1, 4 bits wide
  assign xor_1_out = {A3, A2, A1, A0} ^ {B3, B2, B1, B0};  // XOR_Gate xor_1, 4 bits wide
  assign not_1_out = ~{A3, A2, A1, A0};  // NOT_Gate not_1, 4 bits wide
  Multiplexer #(.select(2), .width(4)) multiplexer_1 (
    .in0(and_1_out), .in1(or_1_out), .in2(xor_1_out), .in3(not_1_out), .out(out_11), .sel({S0, Cin}));  // open: en

  // Notes on the sheet:
  //   A
  //   B
  //   A
  //   B
endmodule

module ALU (
  input  A3,
  input  A2,
  input  A1,
  input  A0,
  input  B3,
  input  B2,
  input  B1,
  input  B0,
  input  Cin,
  input  S2,
  input  S1,
  input  S0,
  output [3:0] Result
);

  wire adder_2_c, adder_3_c, adder_4_c;
  wire [3:0] adder_4_s, logic_1_out_11, multiplexer_1_out, shifter_1_out_9;

  \logic  logic_1 (
    .A3(A3), .A2(A2), .A1(A1), .A0(A0), .out_11(logic_1_out_11), .B3(B3), .S0(S0), .B2(B2), .B1(B1),
    .Cin(Cin), .B0(B0));
  shifter shifter_1 (
    .A3(B3), .A2(B2), .A1(B1), .A0(B0), .So(S0), .Cin(Cin), .out_7(shifter_1_out_9[3]),
    .out_8(shifter_1_out_9[2]), .out_9(shifter_1_out_9[0]), .out_10(shifter_1_out_9[1]));
  adder adder_1 (.S(adder_4_s[3]), .Ai(A3), .Bi(B3), .Ci(adder_2_c), .S1(S1), .S0(S0));  // open: C
  adder adder_2 (.S(adder_4_s[2]), .Ai(A2), .Bi(B2), .Ci(adder_3_c), .C(adder_2_c), .S1(S1), .S0(S0));
  adder adder_3 (.S(adder_4_s[1]), .Ai(A1), .Bi(B1), .Ci(adder_4_c), .C(adder_3_c), .S1(S1), .S0(S0));
  adder adder_4 (.S(adder_4_s[0]), .Ai(A0), .Bi(B0), .Ci(Cin), .C(adder_4_c), .S1(S1), .S0(S0));
  Multiplexer #(.width(4)) multiplexer_1 (
    .in0(logic_1_out_11), .in1(shifter_1_out_9), .out(multiplexer_1_out), .sel(S1));  // open: en
  Multiplexer #(.width(4)) multiplexer_2 (
    .in0(adder_4_s), .in1(multiplexer_1_out), .out(Result), .sel(S2));  // open: en

  // Notes on the sheet:
  //   Logic
  //   Input 1
  //   Input 2
  //   Shifter
  //   Select Inputs
  //   Adders
endmodule
